// Logisim project ControlUnit.circ as structural Verilog
module ControlUnit (
  input  [31:0] instr,
  input  in_2,
  output [3:0] ALUOp,
  output ALUSrc,
  output Branch,
  output Jump,
  output MemRead,
  output MemWrite,
  output PCSrc,
  output RegWrite,
  output MemToReg
);

  wire and_1_out, and_2_out, and_3_out, and_4_out, and_5_out, and_6_out, and_7_out, and_8_out, and_10_out,
       and_11_out, and_12_out, and_13_out, and_14_out, and_15_out, and_16_out, and_17_out, and_18_out,
       and_19_out, and_20_out, and_21_out, and_22_out, and_23_out, and_24_out, and_25_out, and_26_out,
       and_27_out, and_28_out, and_29_out, and_30_out, and_31_out, and_32_out, and_33_out, and_34_out,
       and_35_out, and_36_out, and_37_out, and_38_out, and_39_out, and_40_out, and_41_out, and_42_out,
       and_43_out, B_Type, comparator_1_eq, comparator_2_eq, comparator_3_eq, comparator_4_eq,
       demultiplexer_1_out1, demultiplexer_1_out2, demultiplexer_1_out3, I_Type, not_1_out, not_2_out,
       not_3_out, not_4_out, or_5_out, or_6_out, R_Type;
  wire [1:0] Type;
  wire [3:0] bit_extender_1_out, bit_extender_2_out, transistor_3_out, transistor_4_out;

  and and_1 (and_1_out, instr[0], instr[1], ~instr[2], ~instr[3]);  // AND_Gate
  and and_2 (and_2_out, instr[4], instr[5], ~instr[6]);  // AND_Gate
  and and_3 (and_3_out, instr[4], ~instr[5], ~instr[6]);  // AND_Gate
  and and_4 (and_4_out, ~instr[4], ~instr[5], ~instr[6]);  // AND_Gate
  and and_5 (and_5_out, ~instr[4], instr[5], ~instr[6]);  // AND_Gate
  and and_6 (and_6_out, ~instr[4], instr[5], instr[6]);  // AND_Gate
  and and_7 (and_7_out, instr[6], instr[5], ~instr[4]);  // AND_Gate
  and and_8 (and_8_out, instr[3], instr[2], instr[1], instr[0]);
  and and_9 (R_Type, and_1_out, and_2_out);
  and and_10 (and_10_out, and_1_out, and_3_out);
  and and_11 (and_11_out, and_1_out, and_4_out);
  and and_12 (and_12_out, and_1_out, and_5_out);
  and and_13 (and_13_out, and_1_out, and_6_out);
  and and_14 (and_14_out, and_7_out, and_8_out);
  Multiplexer #(.select(3), .enable("false")) multiplexer_1 (
    .in0(and_11_out), .in1(and_10_out), .in2(1'b0), .in3(R_Type), .in4(1'b0), .in5(1'b0), .in6(1'b0),
    .in7(1'b0), .out(RegWrite), .sel(instr[6:4]));
  Multiplexer #(.select(3), .enable("false")) multiplexer_2 (
    .in0(and_11_out), .in1(and_10_out), .in2(and_12_out), .in3(1'b0), .in4(1'b0), .in5(1'b0),
    .in6(and_13_out), .in7(1'b0), .out(ALUSrc), .sel(instr[6:4]));
  or or_1 (I_Type, and_10_out, and_11_out, and_12_out);
  Multiplexer #(.select(3), .enable("false")) multiplexer_3 (
    .in0(and_11_out), .in1(1'b0), .in2(1'b0), .in3(1'b0), .in4(1'b0), .in5(1'b0), .in6(1'b0), .in7(1'b0),
    .out(MemRead), .sel(instr[6:4]));
  Multiplexer #(.select(3), .enable("false")) multiplexer_4 (
    .in0(and_11_out), .in1(1'b0), .in2(1'b0), .in3(1'b0), .in4(1'b0), .in5(1'b0), .in6(1'b0), .in7(1'b0),
    .out(MemToReg), .sel(instr[6:4]));
  Multiplexer #(.select(3), .enable("false")) multiplexer_5 (
    .in0(1'b0), .in1(1'b0), .in2(and_12_out), .in3(1'b0), .in4(1'b0), .in5(1'b0), .in6(1'b0), .in7(1'b0),
    .out(MemWrite), .sel(instr[6:4]));
  Multiplexer #(.select(3), .enable("false")) multiplexer_6 (
    .in0(1'b0), .in1(1'b0), .in2(1'b0), .in3(1'b0), .in4(1'b0), .in5(1'b0), .in6(and_13_out), .in7(1'b0),
    .out(PCSrc), .sel(instr[6:4]));
  Multiplexer #(.select(3), .enable("false")) multiplexer_7 (
    .in0(1'b0), .in1(1'b0), .in2(1'b0), .in3(1'b0), .in4(1'b0), .in5(1'b0), .in6(and_14_out), .in7(1'b0),
    .out(Jump), .sel(instr[6:4]));
  or or_2 (B_Type, and_13_out, and_14_out);
  or or_3 (Type[0], R_Type, B_Type);
  or or_4 (Type[1], I_Type, B_Type);
  Demultiplexer #(.select(2), .enable("false")) demultiplexer_1 (
    .out1(demultiplexer_1_out1), .out2(demultiplexer_1_out2), .out3(demultiplexer_1_out3), .in(in_2),
    .sel(Type));  // open: out0
  Comparator #(.width(7), .mode("unsigned")) comparator_1 (
    .a(instr[6:0]), .b(7'b0100011), .eq(comparator_1_eq));  // open: gt, lt
  Comparator #(.width(7), .mode("unsigned")) comparator_2 (
    .a(instr[6:0]), .b(7'b0000011), .eq(comparator_2_eq));  // open: gt, lt
  Comparator #(.width(7), .mode("unsigned")) comparator_3 (
    .a(instr[6:0]), .b(7'b1101111), .eq(comparator_3_eq));  // open: gt, lt
  Comparator #(.width(7), .mode("unsigned")) comparator_4 (
    .a(instr[6:0]), .b(7'b0000011), .eq(comparator_4_eq));  // open: gt, lt
  or or_5 (or_5_out, comparator_1_eq, comparator_2_eq);
  or or_6 (or_6_out, comparator_3_eq, comparator_4_eq);
  and and_15 (and_15_out, ~instr[25], ~instr[26], ~instr[27], ~instr[28], ~instr[29], ~instr[30], ~instr[31]);  // AND_Gate
  and and_16 (and_16_out, ~instr[12], ~instr[13], ~instr[14]);  // AND_Gate
  and and_17 (and_17_out, instr[12], instr[13], instr[14]);
  and and_18 (and_18_out, ~instr[12], instr[13], instr[14]);  // AND_Gate
  and and_19 (and_19_out, ~instr[12], ~instr[13], instr[14]);  // AND_Gate
  and and_20 (and_20_out, instr[12], ~instr[13], ~instr[14]);  // AND_Gate
  and and_21 (and_21_out, instr[12], ~instr[13], instr[14]);  // AND_Gate
  and and_22 (and_22_out, ~instr[12], instr[13], ~instr[14]);  // AND_Gate
  and and_23 (and_23_out, instr[12], instr[13], ~instr[14]);  // AND_Gate
  and and_24 (and_24_out, ~instr[25], ~instr[26], ~instr[27], ~instr[28], ~instr[29], instr[30], ~instr[31]);  // AND_Gate
  and and_25 (and_25_out, ~instr[12], ~instr[13], ~instr[14]);  // AND_Gate
  and and_26 (and_26_out, instr[12], ~instr[13], instr[14]);  // AND_Gate
  and and_27 (and_27_out, instr[25], ~instr[26], ~instr[27], ~instr[28], ~instr[29], ~instr[30], ~instr[31]);  // AND_Gate
  and and_28 (and_28_out, ~instr[12], ~instr[13], ~instr[14]);  // AND_Gate
  and and_29 (and_29_out, ~instr[12], ~instr[13], instr[14]);  // AND_Gate
  assign bit_extender_1_out = {{3{1'b0}}, not_1_out};  // Bit_Extender bit_extender_1
  not not_1 (not_1_out, or_5_out);
  not not_2 (not_2_out, or_5_out);
  assign bit_extender_2_out = {{3{1'b0}}, not_3_out};  // Bit_Extender bit_extender_2
  not not_3 (not_3_out, or_6_out);
  not not_4 (not_4_out, or_6_out);
  and and_30 (and_30_out, and_15_out, and_16_out);
  and and_31 (and_31_out, and_15_out, and_17_out);
  and and_32 (and_32_out, and_15_out, and_18_out);
  and and_33 (and_33_out, and_15_out, and_19_out);
  and and_34 (and_34_out, and_15_out, and_20_out);
  and and_35 (and_35_out, and_15_out, and_21_out);
  and and_36 (and_36_out, and_15_out, and_22_out);
  and and_37 (and_37_out, and_15_out, and_23_out);
  and and_38 (and_38_out, and_24_out, and_25_out);
  and and_39 (and_39_out, and_24_out, and_26_out);
  and and_40 (and_40_out, and_27_out, and_28_out);
  and and_41 (and_41_out, and_27_out, and_29_out);
  and and_42 (and_42_out, not_2_out, demultiplexer_1_out2);
  and and_43 (and_43_out, not_4_out, demultiplexer_1_out3);
  Transistor #(.\type ("n"), .gate("br"), .width(4)) transistor_1 (
    .in(bit_extender_1_out), .out(ALUOp), .gate(or_5_out));
  Transistor #(.\type ("n"), .gate("br"), .width(4)) transistor_2 (
    .in(bit_extender_2_out), .out(ALUOp), .gate(or_6_out));
  Transistor #(.\type ("n"), .width(4)) transistor_3 (.in(4'b0000), .out(transistor_3_out), .gate(and_30_out));
  Transistor #(.\type ("n"), .gate("br"), .width(4)) transistor_4 (
    .in(4'b0000), .out(transistor_4_out), .gate(and_16_out));
  Transistor #(.\type ("n"), .width(4)) transistor_5 (.in(4'b0100), .out(transistor_3_out), .gate(and_31_out));
  Transistor #(.\type ("n"), .gate("br"), .width(4)) transistor_6 (
    .in(4'b0100), .out(transistor_4_out), .gate(and_17_out));
  Transistor #(.\type ("n"), .width(4)) transistor_7 (.in(4'b1000), .out(transistor_3_out), .gate(and_32_out));
  Transistor #(.\type ("n"), .gate("br"), .width(4)) transistor_8 (
    .in(4'b1000), .out(transistor_4_out), .gate(and_18_out));
  Transistor #(.\type ("n"), .width(4)) transistor_9 (.in(4'b1001), .out(transistor_3_out), .gate(and_33_out));
  Transistor #(.\type ("n"), .gate("br"), .width(4)) transistor_10 (
    .in(4'b1001), .out(transistor_4_out), .gate(and_19_out));
  Transistor #(.\type ("n"), .width(4)) transistor_11 (.in(4'b1010), .out(transistor_3_out), .gate(and_34_out));
  Transistor #(.\type ("n"), .gate("br"), .width(4)) transistor_12 (
    .in(4'b1010), .out(transistor_4_out), .gate(and_34_out));
  Transistor #(.\type ("n"), .width(4)) transistor_13 (.in(4'b1011), .out(transistor_3_out), .gate(and_35_out));
  Transistor #(.\type ("n"), .gate("br"), .width(4)) transistor_14 (
    .in(4'b1011), .out(transistor_4_out), .gate(and_35_out));
  Transistor #(.\type ("n"), .width(4)) transistor_15 (.in(4'b1101), .out(transistor_3_out), .gate(and_36_out));
  Transistor #(.\type ("n"), .gate("br"), .width(4)) transistor_16 (
    .in(4'b1101), .out(transistor_4_out), .gate(and_22_out));
  Transistor #(.\type ("n"), .width(4)) transistor_17 (.in(4'b1110), .out(transistor_3_out), .gate(and_37_out));
  Transistor #(.\type ("n"), .gate("br"), .width(4)) transistor_18 (
    .in(4'b1110), .out(transistor_4_out), .gate(and_23_out));
  Transistor #(.\type ("n"), .width(4)) transistor_19 (.in(4'b0001), .out(transistor_3_out), .gate(and_38_out));
  Transistor #(.\type ("n"), .width(4)) transistor_20 (.in(4'b1100), .out(transistor_3_out), .gate(and_39_out));
  Transistor #(.\type ("n"), .gate("br"), .width(4)) transistor_21 (
    .in(4'b1100), .out(transistor_4_out), .gate(and_39_out));
  Transistor #(.\type ("n"), .width(4)) transistor_22 (.in(4'b0010), .out(transistor_3_out), .gate(and_40_out));
  Transistor #(.\type ("n"), .width(4)) transistor_23 (.in(4'b0011), .out(transistor_3_out), .gate(and_41_out));
  Transistor #(.\type ("n"), .gate("br"), .width(4)) transistor_24 (
    .in(transistor_3_out), .out(ALUOp), .gate(demultiplexer_1_out1));
  Transistor #(.\type ("n"), .gate("br"), .width(4)) transistor_25 (
    .in(transistor_4_out), .out(ALUOp), .gate(and_42_out));
  Transistor #(.\type ("n"), .gate("br"), .width(4)) transistor_26 (.in(4'b0001), .out(ALUOp), .gate(and_43_out));

  // Other names for the same wires on the sheet: OpCode[6:0] = instr[6:0]; OpCode4[3:0] = instr[3:0];
  //   OpCode3[2:0] = instr[6:4]; funct3[2:0] = instr[14:12]; funct7[6:0] = instr[31:25]

  // Notes on the sheet:
  //   Entradas
  //   Salidas
  //   Type-R
  //   Type-I
  //   Load
  //   Store
  //   Branch
  //   Jump
  //   Funct7 = 0000000
  //   Funct7 = 0100000
  //   Funct7 = 0000001
  //   STORE
  //   LOAD
  //   JUMP/JAL
  //   LOAD
  //   ADD
  //   ADDI
  //   AND
  //   ANDI
  //   OR
  //   ORI
  //   XOR
  //   XORI
  //   SLL
  //   SRL
  //   SLT
  //   SLTI
  //   SLTU
  //   SLTUI
  //   SUB
  //   SRA
  //   MUL
  //   DIV
  //   SLLI
  //   SRLI
  //   SRAI
  //   BRANCH
endmodule
