// Logisim project Pipelined.circ as structural Verilog: 5 circuits, main circuit Pipeline
module Pipeline (
  input  in_1
);

  wire alu_1_zero, Clock, EX_MEM_mem_zero;
  wire [4:0] EX_MEM_mem_write_register, ID_EX_ex_write_register;
  wire [31:0] adder_1_out, adder_2_out, alu_1_resultado, bit_extender_1_out, bit_extender_2_out,
       bit_extender_3_out, bit_extender_4_out, Data_Memory_data, EX_MEM_mem_address, EX_MEM_mem_pc___4,
       EX_MEM_mem_write_data, ID_EX_ex_imm_branch, ID_EX_ex_imm_jump, ID_EX_ex_imm_lw_xl, ID_EX_ex_imm_sw,
       ID_EX_ex_pc___4, ID_EX_ex_rs1, ID_EX_ex_rs2, IF_ID_id_instruction, IF_ID_id_pc___4,
       Instruction_Memory_data, MEM_WEB_wb_address, MEM_WEB_wb_read_data, multiplexer_1_out,
       multiplexer_2_out, multiplexer_3_out, multiplexer_4_out, PC_q, registerfile_1_d1, registerfile_1_d2;

  Clock clock_1 (.out(Clock));
  Multiplexer #(.width(32), .enable("false")) multiplexer_1 (
    .in0(adder_1_out), .in1(EX_MEM_mem_pc___4), .out(multiplexer_1_out), .sel(in_1));
  Register #(.width(32), .Select("low")) PC (.D(multiplexer_1_out), .Q(PC_q), .clk(Clock));  // open: en, clr
  Adder #(.width(32)) adder_1 (.a(32'h4), .b(PC_q), .out(adder_1_out));  // open: cin, cout
  ROM #(.dataWidth(32), .Select("low")) Instruction_Memory (.addr(PC_q[9:2]), .data(Instruction_Memory_data));
  IF_ID IF_ID (
    .IF_PC___4(adder_1_out), .IF_Instruction(Instruction_Memory_data), .Clock(Clock),
    .ID_PC___4(IF_ID_id_pc___4), .ID_Instruction(IF_ID_id_instruction));
  assign bit_extender_1_out = {{20{1'b0}}, IF_ID_id_instruction[31:20]};  // Bit_Extender bit_extender_1
  assign bit_extender_2_out = {{20{1'b0}}, {IF_ID_id_instruction[31:25], IF_ID_id_instruction[11:7]}};  // Bit_Extender bit_extender_2
  assign bit_extender_3_out = {{20{1'b0}}, {IF_ID_id_instruction[31], IF_ID_id_instruction[7], IF_ID_id_instruction[30:26], IF_ID_id_instruction[11:8], 1'b0}};  // Bit_Extender bit_extender_3
  assign bit_extender_4_out = {{11{1'b0}}, {IF_ID_id_instruction[31], IF_ID_id_instruction[19:12], IF_ID_id_instruction[20], IF_ID_id_instruction[30:21], 1'b0}};  // Bit_Extender bit_extender_4
  RegisterFile registerfile_1 (
    .Clock(Clock), .rs1(IF_ID_id_instruction[19:15]), .rs2(IF_ID_id_instruction[24:20]),
    .Write_register(IF_ID_id_instruction[11:7]), .Write_data(multiplexer_4_out), .d1(registerfile_1_d1),
    .d2(registerfile_1_d2));  // open: RegWrite
  ID_EX ID_EX (
    .ID_PC___4(IF_ID_id_pc___4), .ID_rs1(registerfile_1_d1), .ID_rs2(registerfile_1_d2),
    .ID_Imm_LW_xl(bit_extender_1_out), .ID_Imm_SW(bit_extender_2_out), .ID_Imm_Branch(bit_extender_3_out),
    .ID_Imm_Jump(bit_extender_4_out), .in_9(Clock), .EX_PC___4(ID_EX_ex_pc___4), .EX_rs1(ID_EX_ex_rs1),
    .EX_rs2(ID_EX_ex_rs2), .EX_Imm_LW_xl(ID_EX_ex_imm_lw_xl), .EX_Imm_SW(ID_EX_ex_imm_sw),
    .EX_Imm_Branch(ID_EX_ex_imm_branch), .EX_Imm_Jump(ID_EX_ex_imm_jump),
    .ID_Write_Register(IF_ID_id_instruction[11:7]), .EX_Write_Register(ID_EX_ex_write_register));
  Multiplexer #(.width(32), .enable("false")) multiplexer_2 (
    .in0(ID_EX_ex_rs2), .in1(multiplexer_3_out), .out(multiplexer_2_out));  // open: sel
  Multiplexer #(.select(2), .width(32), .enable("false")) multiplexer_3 (
    .in0(ID_EX_ex_imm_lw_xl), .in1(ID_EX_ex_imm_sw), .in2(ID_EX_ex_imm_branch), .in3(ID_EX_ex_imm_jump),
    .out(multiplexer_3_out));  // open: sel
  Adder #(.width(32)) adder_2 (.a(ID_EX_ex_pc___4), .b(ID_EX_ex_imm_branch), .out(adder_2_out));  // open: cin, cout
  ALU alu_1 (
    .Operand1__rs1(ID_EX_ex_rs1), .Operand2__rs2(multiplexer_2_out), .Clock(Clock),
    .Resultado(alu_1_resultado), .Zero(alu_1_zero));  // open: Control
  EX_MEM EX_MEM (
    .EX_PC___4(adder_2_out), .EX_Zero(alu_1_zero), .EX_Address(alu_1_resultado),
    .EX_Write_Data(ID_EX_ex_rs2), .EX_Write_Register(ID_EX_ex_write_register), .Clock(Clock),
    .MEM_PC___4(EX_MEM_mem_pc___4), .MEM_Zero(EX_MEM_mem_zero), .MEM_Address(EX_MEM_mem_address),
    .MEM_Write_Data(EX_MEM_mem_write_data), .MEM_Write_Register(EX_MEM_mem_write_register));
  RAM #(.dataWidth(32), .bus("separate"), .Select("low")) Data_Memory (
    .addr(EX_MEM_mem_address[7:0]), .din(EX_MEM_mem_write_data), .data(Data_Memory_data), .clk(Clock));  // open: str, sel, ld, clr
  MEM_WB MEM_WEB (
    .MEM_Read_Data(Data_Memory_data), .MEM_Address(EX_MEM_mem_address),
    .MEM_Write_Register(EX_MEM_mem_write_register), .Clock(Clock), .WB_Read_Data(MEM_WEB_wb_read_data),
    .WB_Address(MEM_WEB_wb_address), .WB_Write_Register(IF_ID_id_instruction[11:7]));
  Multiplexer #(.width(32), .enable("false")) multiplexer_4 (
    .in0(MEM_WEB_wb_read_data), .in1(MEM_WEB_wb_address), .out(multiplexer_4_out));  // open: sel

  // Notes on the sheet:
  //   I-Type
  //   S-Type
  //   Branch
  //   Jump
  //   Write Register
endmodule

module IF_ID (
  input  [31:0] IF_PC___4,
  input  [31:0] IF_Instruction,
  input  Clock,
  output [31:0] ID_PC___4,
  output [31:0] ID_Instruction
);

  Register #(.width(32), .Select("low")) register_1 (.D(IF_PC___4), .Q(ID_PC___4), .clk(Clock));  // open: en, clr
  Register #(.width(32), .Select("low")) register_2 (
    .D(IF_Instruction), .Q(ID_Instruction), .clk(Clock));  // open: en, clr

  // Other names for the same wires on the sheet: ID_Instr[31:0] = ID_Instruction; ID_PC_4[31:0] = ID_PC___4;
  //   IF_Instr[31:0] = IF_Instruction; IF_PC_4[31:0] = IF_PC___4

  // Notes on the sheet:
  //   Control
endmodule

module ID_EX (
  input  [31:0] ID_PC___4,
  input  [31:0] ID_rs1,
  input  [31:0] ID_rs2,
  input  [31:0] ID_Imm_LW_xl,
  input  [31:0] ID_Imm_SW,
  input  [31:0] ID_Imm_Branch,
  input  [31:0] ID_Imm_Jump,
  input  [4:0] ID_Write_Register,
  input  in_9,
  output [31:0] EX_PC___4,
  output [31:0] EX_rs1,
  output [31:0] EX_rs2,
  output [31:0] EX_Imm_LW_xl,
  output [31:0] EX_Imm_SW,
  output [31:0] EX_Imm_Branch,
  output [31:0] EX_Imm_Jump,
  output [4:0] EX_Write_Register
);

  Register #(.width(32), .Select("low")) register_1 (.D(ID_PC___4), .Q(EX_PC___4), .clk(in_9));  // open: en, clr
  Register #(.width(32), .Select("low")) register_2 (.D(ID_rs1), .Q(EX_rs1), .clk(in_9));  // open: en, clr
  Register #(.width(32), .Select("low")) register_3 (.D(ID_rs2), .Q(EX_rs2), .clk(in_9));  // open: en, clr
  Register #(.width(32), .Select("low")) register_4 (.D(ID_Imm_LW_xl), .Q(EX_Imm_LW_xl), .clk(in_9));  // open: en, clr
  Register #(.width(32), .Select("low")) register_5 (.D(ID_Imm_SW), .Q(EX_Imm_SW), .clk(in_9));  // open: en, clr
  Register #(.width(32), .Select("low")) register_6 (
    .D(ID_Imm_Branch), .Q(EX_Imm_Branch), .clk(in_9));  // open: en, clr
  Register #(.width(32), .Select("low")) register_7 (.D(ID_Imm_Jump), .Q(EX_Imm_Jump), .clk(in_9));  // open: en, clr
  Register #(.width(5), .Select("low")) register_8 (
    .D(ID_Write_Register), .Q(EX_Write_Register), .clk(in_9));  // open: en, clr

  // Other names for the same wires on the sheet: Clock = in_9

  // Notes on the sheet:
  //   Entradas
  //   Salidas
endmodule

module EX_MEM (
  input  [31:0] EX_PC___4,
  input  EX_Zero,
  input  [31:0] EX_Address,
  input  [31:0] EX_Write_Data,
  input  [4:0] EX_Write_Register,
  input  Clock,
  output [31:0] MEM_PC___4,
  output MEM_Zero,
  output [31:0] MEM_Address,
  output [31:0] MEM_Write_Data,
  output [4:0] MEM_Write_Register
);

  Register #(.width(32), .Select("low")) register_1 (.D(EX_PC___4), .Q(MEM_PC___4), .clk(Clock));  // open: en, clr
  Register #(.width(1), .Select("low")) register_2 (.D(EX_Zero), .Q(MEM_Zero), .clk(Clock));  // open: en, clr
  Register #(.width(32), .Select("low")) register_3 (.D(EX_Address), .Q(MEM_Address), .clk(Clock));  // open: en, clr
  Register #(.width(32), .Select("low")) register_4 (
    .D(EX_Write_Data), .Q(MEM_Write_Data), .clk(Clock));  // open: en, clr
  Register #(.width(5), .Select("low")) register_5 (
    .D(EX_Write_Register), .Q(MEM_Write_Register), .clk(Clock));  // open: en, clr
endmodule

module MEM_WB (
  input  [31:0] MEM_Read_Data,
  input  [31:0] MEM_Address,
  input  [4:0] MEM_Write_Register,
  input  Clock,
  output [31:0] WB_Read_Data,
  output [31:0] WB_Address,
  output [4:0] WB_Write_Register
);

  Register #(.width(32), .Select("low")) register_1 (
    .D(MEM_Read_Data), .Q(WB_Read_Data), .clk(Clock));  // open: en, clr
  Register #(.width(32), .Select("low")) register_2 (.D(MEM_Address), .Q(WB_Address), .clk(Clock));  // open: en, clr
  Register #(.width(5), .Select("low")) register_3 (
    .D(MEM_Write_Register), .Q(WB_Write_Register), .clk(Clock));  // open: en, clr
endmodule
