// Logisim project CPU_B94560.circ as structural Verilog
module main (
  input  RegWrite
);

  wire Clock_out, fivestagesclock_1_clock_1, fivestagesclock_1_clock_2, fivestagesclock_1_clock_3,
       fivestagesclock_1_clock_4, fivestagesclock_1_clock_5, fivestagesclock_1_start, or_1_out;
  wire [7:0] register_5_q;
  wire [31:0] adder_1_out, ALU_resultado, bit_extender_1_out, bit_extender_2_out, bit_extender_3_out,
       Instruction_memory_data, multiplexer_1_out, multiplexer_2_out, multiplexer_3_out, PC_q, ram_1_data,
       register_1_q, register_2_q, register_3_q, register_4_q, register_6_q, registerfile_1_d1,
       registerfile_1_d2;
  wire [31:8] register_5_q_2;

  Multiplexer #(.width(32), .enable("false")) multiplexer_1 (
    .in0(adder_1_out), .out(multiplexer_1_out), .sel(1'b0));  // open: in1
  Register #(.width(32), .Select("low")) PC (
    .D(multiplexer_1_out), .Q(PC_q), .clk(fivestagesclock_1_clock_1), .clr(fivestagesclock_1_start));  // open: en
  Clock Clock (.out(Clock_out));
  Adder #(.width(32)) adder_1 (.a(32'h4), .b(PC_q), .out(adder_1_out));  // open: cin, cout
  FiveStagesClock fivestagesclock_1 (
    .in_1(Clock_out), .Start(fivestagesclock_1_start), .Clock_1(fivestagesclock_1_clock_1),
    .Clock_2(fivestagesclock_1_clock_2), .Clock_3(fivestagesclock_1_clock_3),
    .Clock_4(fivestagesclock_1_clock_4), .Clock_5(fivestagesclock_1_clock_5));
  ROM #(.dataWidth(32), .Select("low")) Instruction_memory (.addr(PC_q[9:2]), .data(Instruction_memory_data));
  Register #(.width(32), .Select("low")) register_1 (
    .D(PC_q), .Q(register_1_q), .clk(fivestagesclock_1_clock_2));  // open: en, clr
  Register #(.width(32), .Select("low")) register_2 (
    .D(Instruction_memory_data), .Q(register_2_q), .clk(fivestagesclock_1_clock_2));  // open: en, clr
  assign bit_extender_1_out = {{20{1'b0}}, register_2_q[31:20]};  // Bit_Extender bit_extender_1
  assign bit_extender_2_out = {{20{1'b0}}, {register_2_q[31:25], register_2_q[11:7]}};  // Bit_Extender bit_extender_2
  assign bit_extender_3_out = {{20{1'b0}}, {register_2_q[31], register_2_q[7], register_2_q[30:26], register_2_q[11:8], 1'b0}};  // Bit_Extender bit_extender_3
  RegisterFile_B94560_RegisterFile registerfile_1 (
    .Clock(or_1_out), .RegWrite(RegWrite), .rs1(register_2_q[19:15]), .rs2(register_2_q[24:20]),
    .Write_register(register_2_q[11:7]), .Write_data(register_6_q), .d1(registerfile_1_d1),
    .d2(registerfile_1_d2));
  or or_1 (or_1_out, fivestagesclock_1_clock_3, fivestagesclock_1_clock_5);
  Register #(.width(32), .Select("low")) register_3 (
    .D(registerfile_1_d1), .Q(register_3_q), .clk(fivestagesclock_1_clock_3));  // open: en, clr
  Register #(.width(32), .Select("low")) register_4 (
    .D(registerfile_1_d2), .Q(register_4_q), .clk(fivestagesclock_1_clock_3));  // open: en, clr
  Multiplexer #(.select(2), .width(32), .enable("false")) multiplexer_2 (
    .in0(register_4_q), .in1(bit_extender_1_out), .in2(bit_extender_2_out), .in3(bit_extender_3_out),
    .out(multiplexer_2_out), .sel(2'b00));
  Register #(.width(32), .Select("low")) register_5 (
    .D(ALU_resultado), .Q({register_5_q_2, register_5_q}), .clk(fivestagesclock_1_clock_4));  // open: en, clr
  ALU ALU (
    .Operand1__rs1(register_3_q), .Operand2__rs2(multiplexer_2_out), .Control(4'b0000),
    .Clock(fivestagesclock_1_clock_4), .Resultado(ALU_resultado));  // open: Zero
  RAM #(.dataWidth(32), .Select("low")) ram_1 (.addr(register_5_q), .data(ram_1_data));  // open: sel, clk, ld, clr
  Multiplexer #(.width(32), .enable("false")) multiplexer_3 (
    .in0({register_5_q_2, register_5_q}), .in1(ram_1_data), .out(multiplexer_3_out), .sel(1'b0));
  Register #(.width(32), .Select("low")) register_6 (
    .D(multiplexer_3_out), .Q(register_6_q), .clk(fivestagesclock_1_clock_5));  // open: en, clr

  // Notes on the sheet:
  //   S1
  //   S2
  //   S3
  //   Start
  //   S4
  //   S5
  //   contents of Instruction_memory (hex, n*v repeats v):
  //   7302b3
  //   I-Type
  //   S-Type
  //   B-Type
  //   R-Type
  //   funct
endmodule

module IF_ID (
  input  [31:0] IF_PC_4,
  input  [31:0] IF_Instruction,
  input  Clock,
  output [31:0] ID_PC_4,
  output [31:0] ID_Instruction
);

  Register #(.width(32), .Select("low")) PC_4 (.D(IF_PC_4), .Q(ID_PC_4), .clk(Clock));  // open: en, clr
  Register #(.width(32), .Select("low")) Instruction (
    .D(IF_Instruction), .Q(ID_Instruction), .clk(Clock));  // open: en, clr

  // Notes on the sheet:
  //   Datapath
  //   Entradas
  //   Control
  //   Datapath
endmodule

module FiveStagesClock (
  input  in_1,
  output Start,
  output Clock_1,
  output Clock_2,
  output Clock_3,
  output Clock_4,
  output Clock_5
);

  wire [7:0] counter_1_q, divider_1_rem;

  Counter counter_1 (.Q(counter_1_q), .clk(in_1));  // open: load, D, count, carry, clr, preset, down
  Divider divider_1 (.a(counter_1_q), .b(8'h5), .rem(divider_1_rem));  // open: out, upper
  Demultiplexer #(.select(3), .enable("false")) demultiplexer_1 (
    .out0(Clock_1), .out1(Clock_2), .out2(Clock_3), .out3(Clock_4), .out4(Clock_5), .in(in_1),
    .sel(divider_1_rem[2:0]));  // open: out5, out6, out7
  Comparator comparator_1 (.a({8{1'b0}}), .b(counter_1_q), .eq(Start));  // open: gt, lt

  // Other names for the same wires on the sheet: Clock = in_1

  // Notes on the sheet:
  //   Entrada
  //   Salidas
endmodule
